# Fritzing sketch circuit diagram (saved by Fritzing 0.9.3b)
breadboards: 3

parts:
  Bauteil1 = Arduino Uno (Rev3)
  BLUE = LEDs [package=led10mm]
  R3 = Resistor [tolerance=±5% resistance=560 package="1206 [SMD]"]
  R2 = Resistor [tolerance=±5% resistance=560 package="1206 [SMD]"]
  GREEN = LEDs [package=led10mm]
  RED = LEDs [package=led10mm]
  R1 = Resistor [tolerance=±5% resistance=560 package="1206 [SMD]"]

nets:
  N1: Bauteil1.D8, R3.Pin_0
  N2: Bauteil1.D9_PWM, R2.Pin_0
  N3: Bauteil1.D10_PWM/SS, R1.Pin_0
  N4: Bauteil1.GND, BLUE.C, GREEN.C, RED.C
  N5: BLUE.A, R3.Pin_1
  N6: R2.Pin_1, GREEN.A
  N7: RED.A, R1.Pin_1
